# Fritzing sketch Gyrophare (saved by Fritzing 0.9.3b)
breadboards: 1

parts:
  WeMos_D1_Mini_Protoboard_Shield1 = WeMos D1 Mini Protoboard Shield
  WeMos_D1_Mini1 = WeMos D1 Mini
  IC1 = ULN2803A [package=THT]
  J1 = Piezo Speaker
  LED2 = LED - 5mm [color="White (4500K)" package="5 mm [THT]"]
  R1 = Resistor [tolerance=±5% resistance=220 package=THT]
  M1 = DC Motor
  C1 = Electrolytic Capacitor [capacitance=0.22mF package="100 mil [THT, electrolytic]"]

nets:
  N1: WeMos_D1_Mini_Protoboard_Shield1.D2, WeMos_D1_Mini_Protoboard_Shield1.X7-Y4, IC1.In_6
  N2: WeMos_D1_Mini_Protoboard_Shield1.D3, WeMos_D1_Mini_Protoboard_Shield1.X7-Y5, IC1.In_7
  N3: WeMos_D1_Mini_Protoboard_Shield1.D4, WeMos_D1_Mini_Protoboard_Shield1.X7-Y6, IC1.In_8
  N4: WeMos_D1_Mini_Protoboard_Shield1.G, WeMos_D1_Mini_Protoboard_Shield1.X7-Y7, IC1.0V
  N5: WeMos_D1_Mini1.5V, IC1.COM_-_Common, J1.pin2, LED2.anode, M1.pin_1, C1.+
  N6: IC1.Out_8, J1.pin1
  N7: IC1.Out_7, R1.Pin_0
  N8: IC1.Out_6, M1.pin_2, C1.-
  N9: LED2.cathode, R1.Pin_1
